# Fritzing sketch whac_the_mole (saved by Fritzing 0.9.3b)
breadboards: 1

parts:
  Part1 = Arduino Uno (Rev3)
  Part2 = Arduino Nano (Rev3.0)

nets:
  N1: Part1.A0, Part2.D8
  N2: Part1.A1, Part2.D9
  N3: Part1.A2, Part2.D10
  N4: Part1.A3, Part2.D11/MOSI
  N5: Part1.A4/SDA, Part2.D12/MISO
  N6: Part1.D8, Part2.D1/TX
  N7: Part1.D9_PWM, Part2.D0/RX
  N8: Part1.D13/SCK, Part2.D13/SCK
  N9: Part1.D2, Part2.D2
  N10: Part1.D3_PWM, Part2.D3
  N11: Part1.D4, Part2.D4
  N12: Part1.D5_PWM, Part2.D5
  N13: Part1.D6_PWM, Part2.D6
  N14: Part1.D7, Part2.D7
  5V: Part1.5V, Part2.VIN
  GND: Part1.GND, Part2.GND
